# Fritzing sketch Arduino_Steering (saved by Fritzing 0.9.3b)
breadboards: 1

parts:
  Part3 = Arduino Uno (Rev3)
  Mod2 = JRPR921X
  U4 = LIPO-2000mAh [package=lipo-2000]
  U5 = Molex Picoblade Series Header [part_number=0532610519 package=Picoblade-53261-0519]
  U6 = Molex Picoblade Series Header [part_number=0532610519 package=Picoblade-53261-0519]
  M5 = RioRand LM2596
  M6 = RioRand LM2596
  DRV_2 = DRV 8825 Stepper Motor Carrier, High Current [part_number="DRV 8825"]
  Part4 = Arduino Nano (Rev3.0) (ICSP)
  M7 = Stepper Motor - Bipolar
  A6 = MakerHawk optical endstop
  A7 = MakerHawk optical endstop
  A8 = MakerHawk optical endstop
  A9 = ZS-X10 motor driver
  A10 = ZS-X10 motor driver

nets:
  N1: Part3.A4/SDA, U5.2
  N2: Part3.A5/SCL, U5.1
  N3: Part3.D8, A9.Pin_18
  N4: Part3.GND, Mod2.THRO-1, Mod2.GEAR-1, Mod2.AUX4-1, U5.4, M5.Pin_4, A9.Pin_11, A9.Pin_19, A10.Pin_6, A10.Pin_19
  N5: Part3.D2, Mod2.THRO-3
  N6: Part3.D3_PWM, Mod2.AUX1-3
  N7: Part3.D5_PWM, A10.Pin_13
  N8: Part3.D6_PWM, A9.Pin_13
  N9: Part3.D7, A10.Pin_18
  N10: Part3.5V, Mod2.THRO-2, Mod2.AUX4-2
  N11: Part3.VIN, U5.5, M5.Pin_3
  N12: Mod2.ALE-SIG, U5.3
  N13: U4.+, M5.Pin_2
  N14: U4.-, M5.Pin_1
  N15: U6.1, Part4.A5
  N16: U6.2, Part4.A4
  N17: U6.3, Part4.D2
  N18: U6.4, M6.Pin_2
  N19: U6.5, M6.Pin_1
  N20: M6.Pin_3, DRV_2.VOLTAGE_DD, Part4.5V, A6.Pin_3, A7.Pin_3, A8.Pin_3
  N21: M6.Pin_4, Part4.VIN
  N22: DRV_2.STEP, Part4.D6
  N23: DRV_2.DIRECTION, Part4.D5
  N24: DRV_2.OUT_2B, M7.A
  N25: DRV_2.OUT_2A, M7.C
  N26: DRV_2.OUT_1A, M7.B
  N27: DRV_2.OUT_1B, M7.D
  N28: DRV_2.GROUND_LOG, Part4.GND, A6.Pin_2, A7.Pin_2, A8.Pin_2
  N29: Part4.D10, A7.Pin_1
  N30: Part4.D11/MOSI, A6.Pin_1
  N31: Part4.D12/MISO, A8.Pin_1

notes:
  +12V RED
  GND BROWN
  D2 - RC signal BLUE
  A4 - SDA GREEN
  A5 - SCL WHITE (Green)
  D2 - Speed / Direction
  D3 - Max Speed? - Optional
  A4 - SDA
  A5 - SCL
  D6 - Left motor speed
  D5 - Right motor speed
  D8 - Left motor direction
  D7 - Right motor direction
  D9 - Stop pin (not used)

custom parts:
  JRPR921X: JRPR921X 9 channel RC receiver. PCB has been omitted as not useful.
  MakerHawk optical endstop: MakerHawk optical endstop.
  ZS-X10 motor driver: DC 6-60V 400W BLDC Three Phase DC Brushless Motor Controller PWM Hall Motor Control Driver Board 12V 24V 48V.
